# Fritzing sketch schematic diagram (saved by Fritzing 0.9.3b)
breadboards: 1

parts:
  Part1 = Arduino Uno (Rev3)
  PIR1 = PIR sensor

nets:
  GND: Part1.GND, PIR1.GND
  N1: Part1.D2, PIR1.SIG
  5V: Part1.5V, PIR1.VDD
